# Fritzing sketch ArduinoUNO_Rev3_ProtoShield (saved by Fritzing 0.9.3b)

parts:
  Bauteil1 = Adafruit Proto Shield for Arduino Kit - v.5
  U1 = FS1000A - 433Mhz RF Transmitter [package=THT]
  TRS1 = Audio Jack (TRS) 3.5mm [package="4Ucon 08780 [THT]"]
  R1 = Resistor [tolerance=±5% resistance=4.7k package="2512 [SMD]"]
  Bauteil2 = Passive Buzzer
  Bauteil3 = Arduino Uno (Rev3) - ICSP  # not connected
  Bauteil4 = DeuLigne 1.1 - The Snootlab's LCD shield for Arduino  # not connected

nets:
  GND: Bauteil1.GND, Bauteil1.P$2, U1.GND
  N1: Bauteil1.P$6#171, Bauteil2.GND
  N2: Bauteil1.P$6#174, Bauteil2.NC
  N3: Bauteil1.N$38, Bauteil1.N$39, TRS1.Ring
  N4: Bauteil1.N$80, TRS1.Sleeve
  N5: Bauteil1.N$102, R1.Pin_0
  N6: Bauteil1.N$136, U1.VCC
  N7: Bauteil1.N$168, U1.DATA
  N8: Bauteil1.N$218, Bauteil1.N$219, TRS1.Tip
  N9: Bauteil1.N$273, R1.Pin_1

custom parts:
  Adafruit Proto Shield for Arduino Kit - v.5: Arduino prototyping shield designed by Adafruit Industries
  FS1000A - 433Mhz RF Transmitter: This is 433Mhz RF transmitter with receiver kit for Arduino ARM MCU wireless Application environment: Remote control switch, receiver module, motorcycles, automobile anti-theft products, home security products, electric doors, shutter doors, windows, remote control socket, remote control LED, remote audio remote control electric doors, garage door remote control, remote control retractable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
